# Fritzing sketch lcd-sketch-fritzing (saved by Fritzing 0.9.4)
breadboards: 1

parts:
  Part1 = Arduino Uno (Rev3) - ICSP
  HD44780U = LCD-16X2 [package=lcd-16x2]
  Contrast = Rotary Potentiometer (Small) [maximum_resistance=100kΩ package=THT]
  Brightness = Rotary Potentiometer (Small) [maximum_resistance=100kΩ package=THT]

nets:
  5V: Part1.5V, HD44780U.VDD, Contrast.leg2, Brightness.leg2
  GND: Part1.GND, HD44780U.VSS, HD44780U.A, Contrast.leg1, Brightness.leg1
  N1: Part1.D8, HD44780U.E
  N2: Part1.D9_PWM, HD44780U.R_W
  N3: Part1.D10_PWM/SS, HD44780U.RS
  N4: Part1.D4, HD44780U.DB4
  N5: Part1.D5_PWM, HD44780U.DB5
  N6: Part1.D6_PWM, HD44780U.DB6
  N7: Part1.D7, HD44780U.DB7
  N8: HD44780U.VO, Contrast.wiper
  N9: HD44780U.K, Brightness.wiper
